// Digital circuit CPU.dig as structural Verilog
module CPU (
  input  clk
);

  wire A_LD_CDATA, IR_LD_XDATA, MAR_LD_CADDR, MBR_LD_XDATA, MBR_OUT_CDATA, not_1_out, PC_INC, PC_OUT_MAR;
  wire [7:0] A, driver_2_out, driver_3_out, IR, MBR, ROM_d;
  wire [15:0] add_1_s, driver_1_out, MAR, PC;

  Seven_Seg_Hex seven_seg_hex_1 (.d(MAR[15:12]), .dp(1'b0));
  Seven_Seg_Hex seven_seg_hex_2 (.d(MAR[7:4]), .dp(1'b0));
  Seven_Seg_Hex seven_seg_hex_3 (.d(MAR[11:8]), .dp(1'b0));
  Seven_Seg_Hex seven_seg_hex_4 (.d(MAR[3:0]), .dp(1'b0));
  Seven_Seg_Hex seven_seg_hex_5 (.d(MBR[3:0]), .dp(1'b0));
  Seven_Seg_Hex seven_seg_hex_6 (.d(MBR[7:4]), .dp(1'b0));
  Register #(.Bits(16)) u_PC (.D(add_1_s), .C(clk), .en(PC_INC), .Q(PC));
  Seven_Seg_Hex seven_seg_hex_7 (.d(PC[11:8]), .dp(1'b0));
  Seven_Seg_Hex seven_seg_hex_8 (.d(PC[15:12]), .dp(1'b0));
  assign driver_1_out = MAR_LD_CADDR ? PC : 16'bz;  // Driver driver_1
  Add #(.Bits(16)) add_1 (.a(PC), .b(16'h1), .c_i(1'b0), .s(add_1_s));  // open: c_o
  Seven_Seg_Hex seven_seg_hex_9 (.d(PC[3:0]), .dp(1'b0));
  Seven_Seg_Hex seven_seg_hex_10 (.d(PC[7:4]), .dp(1'b0));
  Seven_Seg_Hex seven_seg_hex_11 (.d(IR[7:4]), .dp(1'b0));
  Register #(.Bits(16)) u_MAR (.D(driver_1_out), .C(clk), .en(MAR_LD_CADDR), .Q(MAR));
  Seven_Seg_Hex seven_seg_hex_12 (.d(IR[3:0]), .dp(1'b0));
  Seven_Seg_Hex seven_seg_hex_13 (.d(A[7:4]), .dp(1'b0));
  Seven_Seg_Hex seven_seg_hex_14 (.d(A[3:0]), .dp(1'b0));
  ROM #(.AddrBits(16), .Bits(8)) ROM (.A(MAR), .sel(1'b1), .D(ROM_d));
  assign driver_2_out = not_1_out ? ROM_d : 8'bz;  // Driver driver_2
  not not_1 (not_1_out, MAR[15]);
  Register #(.Bits(8)) u_MBR (.D(driver_2_out), .C(clk), .en(MBR_LD_XDATA), .Q(MBR));
  assign driver_3_out = MBR_OUT_CDATA ? MBR : 8'bz;  // Driver driver_3
  // Control_Unit control_unit_1: pin names not known; wires that end beside it: 1'b0, 1'b0, 1'b0, 1'b0, IR, clk, PC_OUT_MAR, MAR_LD_CADDR, IR_LD_XDATA, PC_INC, MBR_LD_XDATA, MBR_OUT_CDATA, A_LD_CDATA
  RAMSinglePortSel #(.AddrBits(16), .Bits(8)) RAM (.A(MAR), .CS(MAR[15]), .WE(1'b0), .OE(MAR[15]), .D(driver_2_out));
  Register #(.Bits(8)) u_IR (.D(driver_2_out), .C(clk), .en(IR_LD_XDATA), .Q(IR));
  Register #(.Bits(8)) u_A (.D(driver_3_out), .C(clk), .en(A_LD_CDATA), .Q(A));
  assign driver_3_out = 1'b0 ? A : 8'bz;  // Driver driver_4

  // Other names for the same wires on the sheet: P0_Clock = clk

  // Notes on the sheet:
  //   MAR
  //   MBR
  //   XADDR
  //   PC
  //   IR
  //   A
  //   contents of ROM (hex, n*v repeats v):
  //   a9,42
  //   XDATA Bus
  //   CDATA Bus
endmodule
